// Logisim project IT012_Lab01_25521134.circ as structural Verilog: 6 circuits, main circuit warmup
module warmup (
  input  A,
  input  B,
  input  C,
  input  D,
  input  X,
  input  Y,
  input  Z,
  input  T,
  output E,
  output F
);

  wire and_1_out, and_2_out, and_3_out, and_4_out, not_1_out, not_2_out, not_3_out, not_4_out, not_5_out,
       not_6_out, or_2_out, or_3_out, or_4_out, or_5_out;

  not not_1 (not_1_out, A);
  not not_2 (not_2_out, B);
  not not_3 (not_3_out, C);
  and and_1 (and_1_out, not_1_out, not_2_out, C);
  and and_2 (and_2_out, not_1_out, B, D);
  and and_3 (and_3_out, not_2_out, C, D);
  and and_4 (and_4_out, B, not_3_out, D);
  or or_1 (F, and_1_out, and_2_out, and_3_out, and_4_out);
  not not_4 (not_4_out, Y);
  not not_5 (not_5_out, X);
  not not_6 (not_6_out, Z);
  or or_2 (or_2_out, Y, Z);
  or or_3 (or_3_out, not_4_out, T);
  or or_4 (or_4_out, not_5_out, T);
  or or_5 (or_5_out, not_5_out, not_4_out, not_6_out);
  and and_5 (E, or_2_out, or_3_out, or_4_out, or_5_out);
endmodule

module TN1 (
  input  A,
  input  B,
  input  C,
  output A_prime,
  output OR,
  output AND,
  output NAND,
  output NOR,
  output XOR3,
  output XOR,
  output NAND3,
  output XNOR,
  output CHAIN
);

  wire X_out;

  nand X (X_out, A, B);
  not not_1 (A_prime, A);
  and and_1 (AND, A, B);
  ExactlyOne xor_1 (.out(XOR3), .in0(A), .in1(B), .in2(C));
  nand nand_1 (NAND3, A, B, C);
  nand Y (CHAIN, X_out, C);
  or or_1 (OR, A, B);
  nand nand_2 (NAND, A, B);
  nor nor_1 (NOR, A, B);
  xor xor_2 (XOR, A, B);
  xnor xnor_1 (XNOR, A, B);
endmodule

module TN2 (
  input  X,
  input  Y,
  input  Z,
  output EQ1,
  output EQ2,
  output EQ3,
  output EQ4,
  output EQ5
);

  wire and_1_out, and_2_out, and_3_out, and_4_out, and_5_out, and_6_out, nand_1_out, nor_1_out, not_1_out,
       not_2_out, not_3_out, not_4_out, not_5_out, not_6_out, or_1_out, or_2_out, or_3_out, or_4_out,
       or_5_out, or_6_out;

  not not_1 (not_1_out, X);
  not not_2 (not_2_out, X);
  nor nor_1 (nor_1_out, X, Y);
  nand nand_1 (nand_1_out, X, Y);
  or or_1 (or_1_out, X, and_1_out);
  and and_1 (and_1_out, Y, Z);
  and and_2 (and_2_out, not_1_out, Y);
  and and_3 (and_3_out, not_2_out, Y);
  or or_2 (or_2_out, X, and_2_out);
  or or_3 (or_3_out, X, and_3_out);
  xnor xnor_1 (EQ1, nor_1_out, and_4_out);
  not not_3 (not_3_out, X);
  not not_4 (not_4_out, Y);
  not not_5 (not_5_out, X);
  not not_6 (not_6_out, Y);
  xnor xnor_2 (EQ2, nand_1_out, and_5_out);
  and and_4 (and_4_out, not_3_out, not_4_out);
  and and_5 (and_5_out, not_5_out, not_6_out);
  or or_4 (or_4_out, X, Y);
  and and_6 (and_6_out, or_4_out, or_5_out);
  or or_5 (or_5_out, X, Z);
  or or_6 (or_6_out, X, Y);
  xnor xnor_3 (EQ3, or_1_out, and_6_out);
  xnor xnor_4 (EQ5, or_3_out, or_6_out);
  xnor xnor_5 (EQ4, or_2_out, X);
endmodule

module TN3 (
  input  A,
  input  B,
  input  C,
  input  D,
  output F
);

  wire and_1_out, and_2_out, and_3_out, and_4_out, and_5_out, and_6_out, not_1_out, not_2_out, not_3_out,
       not_4_out;

  not not_1 (not_1_out, B);
  not not_2 (not_2_out, A);
  not not_3 (not_3_out, D);
  not not_4 (not_4_out, C);
  and and_1 (and_1_out, not_2_out, not_1_out, C, not_3_out);
  and and_2 (and_2_out, not_2_out, not_1_out, C, D);
  and and_3 (and_3_out, not_2_out, B, not_4_out, D);
  and and_4 (and_4_out, not_2_out, B, C, D);
  and and_5 (and_5_out, A, not_1_out, C, D);
  and and_6 (and_6_out, A, B, not_4_out, D);
  or or_1 (F, and_1_out, and_2_out, and_3_out, and_4_out, and_5_out, and_6_out);
endmodule

module TN4 (
  input  A,
  input  B,
  input  C,
  input  D,
  output F_can,
  output EQ1,
  output EQ2,
  output F_sop,
  output E_pos
);

  wire and_1_out, and_2_out, and_3_out, and_4_out, and_5_out, and_6_out, and_7_out, and_8_out, and_9_out,
       and_10_out, not_1_out, not_2_out, not_3_out, not_4_out, or_1_out, or_2_out, or_3_out, or_4_out;

  not not_1 (not_1_out, A);
  not not_2 (not_2_out, B);
  not not_3 (not_3_out, D);
  not not_4 (not_4_out, C);
  and and_1 (and_1_out, not_1_out, not_2_out, C, not_3_out);
  and and_2 (and_2_out, not_1_out, not_2_out, C, D);
  and and_3 (and_3_out, not_1_out, B, not_4_out, D);
  and and_4 (and_4_out, not_1_out, B, C, D);
  and and_5 (and_5_out, A, not_2_out, C, D);
  and and_6 (and_6_out, A, B, not_4_out, D);
  and and_7 (and_7_out, not_1_out, not_2_out, C);
  and and_8 (and_8_out, not_1_out, B, D);
  and and_9 (and_9_out, not_2_out, C, D);
  and and_10 (and_10_out, B, not_4_out, D);
  or or_1 (or_1_out, B, C);
  or or_2 (or_2_out, not_2_out, D);
  or or_3 (or_3_out, not_1_out, D);
  or or_4 (or_4_out, not_1_out, not_2_out, not_4_out);
  or or_5 (F_sop, and_7_out, and_8_out, and_9_out, and_10_out);
  and and_11 (E_pos, or_1_out, or_2_out, or_3_out, or_4_out);
  or or_6 (F_can, and_1_out, and_2_out, and_3_out, and_4_out, and_5_out, and_6_out);
  xnor xnor_1 (EQ1, F_can, F_sop);
  xnor xnor_2 (EQ2, F_can, E_pos);
endmodule

module TN5 (
  input  A,
  input  B,
  input  C,
  output F
);

  wire xor_1_out;

  xor xor_1 (xor_1_out, A, B);
  xor xor_2 (F, xor_1_out, C);
endmodule
