// Logisim project IT012_Lab02_25521134.circ as structural Verilog: 9 circuits, main circuit FA
module warmup (
  input  [7:0] A,
  input  [7:0] B,
  output [7:0] S
);

  wire adder_1_cout;

  // Probe on A
  // Probe on B
  Adder adder_1 (.a(A), .b(B), .out(S), .cin(adder_1_cout), .cout(adder_1_cout));
  // Probe on S
endmodule

module FA (
  input  A,
  input  B,
  input  Cin,
  output S,
  output Cout
);

  wire and_1_out, and_2_out, xor_1_out;

  xor xor_1 (xor_1_out, A, B);
  and and_1 (and_1_out, A, B);
  xor xor_2 (S, xor_1_out, Cin);
  and and_2 (and_2_out, Cin, xor_1_out);
  or or_1 (Cout, and_2_out, and_1_out);
endmodule

module ADDSUB4 (
  input  [3:0] A,
  input  [3:0] B,
  input  SUB,
  output [3:0] S,
  output C
);

  wire B_prime_1_out, B_prime_2_out, B_prime_3_out, B_prime_4_out, fa_1_cout, fa_2_cout, fa_3_cout;

  FA fa_1 (.A(A[0]), .B(B_prime_1_out), .Cin(SUB), .S(S[0]), .Cout(fa_1_cout));
  xor B_prime_1 (B_prime_1_out, B[0], SUB);
  // Probe on fa_1_cout
  xor B_prime_2 (B_prime_2_out, B[1], SUB);
  FA fa_2 (.A(A[1]), .B(B_prime_2_out), .Cin(fa_1_cout), .S(S[1]), .Cout(fa_2_cout));
  // Probe on fa_2_cout
  xor B_prime_3 (B_prime_3_out, B[2], SUB);
  FA fa_3 (.A(A[2]), .B(B_prime_3_out), .Cin(fa_2_cout), .S(S[2]), .Cout(fa_3_cout));
  // Probe on fa_3_cout
  xor B_prime_4 (B_prime_4_out, B[3], SUB);
  FA fa_4 (.A(A[3]), .B(B_prime_4_out), .Cin(fa_3_cout), .S(S[3]), .Cout(C));
endmodule

module ALU8 (
  input  [7:0] A,
  input  [7:0] B,
  input  [2:0] OP,
  output [7:0] R,
  output Z,
  output LT
);

  wire subtractor_1_bout, subtractor_2_bout;
  wire [7:0] adder_1_out, adder_2_out, and_1_out, multiplexer_1_out, multiplexer_2_out, not_1_out, or_1_out,
       subtractor_1_out, subtractor_2_out, xor_1_out;

  // Probe on A
  // Probe on B
  Adder adder_1 (.a(A), .b(B), .out(adder_1_out));  // open: cin, cout
  Adder adder_2 (.a(A), .b(8'h1), .out(adder_2_out));  // open: cin, cout
  Subtractor subtractor_1 (.a(A), .b(B), .out(subtractor_1_out), .bout(subtractor_1_bout));  // open: bin
  // Probe on subtractor_1_bout
  Subtractor subtractor_2 (.a(A), .b(8'h1), .out(subtractor_2_out), .bout(subtractor_2_bout));  // open: bin
  // Probe on subtractor_2_bout
  assign and_1_out = A & B;  // AND_Gate and_1, 8 bits wide
  assign or_1_out = A | B;  // OR_Gate or_1, 8 bits wide
  assign not_1_out = ~A;  // NOT_Gate not_1, 8 bits wide
  assign xor_1_out = A ^ B;  // XOR_Gate xor_1, 8 bits wide
  // Probe on multiplexer_1_out
  Multiplexer #(.select(2), .width(8), .enable("false")) multiplexer_1 (
    .in0(adder_1_out), .in1(adder_2_out), .in2(subtractor_1_out), .in3(subtractor_2_out),
    .out(multiplexer_1_out), .sel(OP[1:0]));
  // Probe on OP[1:0]
  // Probe on adder_1_out
  // Probe on adder_2_out
  // Probe on subtractor_1_out
  // Probe on subtractor_2_out
  // Probe on OP[1:0]
  Multiplexer #(.select(2), .width(8), .enable("false")) multiplexer_2 (
    .in0(and_1_out), .in1(or_1_out), .in2(not_1_out), .in3(xor_1_out), .out(multiplexer_2_out), .sel(OP[1:0]));
  // Probe on and_1_out
  // Probe on or_1_out
  // Probe on not_1_out
  // Probe on xor_1_out
  // Probe on multiplexer_2_out
  Multiplexer #(.width(8), .enable("false")) multiplexer_3 (
    .in0(multiplexer_1_out), .in1(multiplexer_2_out), .out(R), .sel(OP[2]));
  // Probe on R
  LT lt_1 (.A7(A[7]), .B7(B[7]), .R7(R[7]), .LT(LT));
  nor nor_1 (Z, R[0], R[1], R[2], R[3], R[4], R[5], R[6], R[7]);
endmodule

module LT (
  input  R7,
  input  A7,
  input  B7,
  output LT
);

  wire not_1_out, xnor_1_out;

  Multiplexer #(.enable("false")) multiplexer_1 (.in0(R7), .in1(A7), .out(LT), .sel(not_1_out));
  xnor xnor_1 (xnor_1_out, B7, A7);
  not not_1 (not_1_out, xnor_1_out);
endmodule

module TN3 (
  input  D,
  input  CLK,
  output Q1,
  output Q2,
  output Q1_prime,
  output Q2_prime
);

  wire d_ff_2_q, LATCH1_q;

  DLATCH dlatch_1 (.D(D), .E(CLK), .Q(Q1));
  D_Flip_Flop d_ff_1 (.clk(CLK), .D(D), .Q(Q2));  // open: Qn, preset, en, reset
  DLATCH LATCH1 (.D(D), .E(CLK), .Q(LATCH1_q));
  D_Flip_Flop d_ff_2 (.clk(CLK), .D(D), .Q(d_ff_2_q));  // open: Qn, preset, en, reset
  DLATCH LATCH2 (.D(LATCH1_q), .E(CLK), .Q(Q1_prime));
  D_Flip_Flop d_ff_3 (.clk(CLK), .D(d_ff_2_q), .Q(Q2_prime));  // open: Qn, preset, en, reset
endmodule

module DLATCH (
  input  D,
  input  E,
  output Q
);

  Multiplexer #(.enable("false")) multiplexer_1 (.in0(Q), .in1(D), .out(Q), .sel(E));
endmodule

module REGFILE (
  input  CLK,
  input  [7:0] DIN,
  input  WE,
  input  [1:0] RA,
  input  [1:0] RD,
  input  [1:0] RB,
  output [7:0] QA,
  output [7:0] QB,
  output [7:0] R0,
  output [7:0] R1,
  output [7:0] R2,
  output [7:0] R3
);

  wire decoder_1_out0, decoder_1_out1, decoder_1_out2, decoder_1_out3;

  // Probe on DIN
  Decoder #(.select(2)) decoder_1 (
    .out0(decoder_1_out0), .out1(decoder_1_out1), .out2(decoder_1_out2), .out3(decoder_1_out3), .sel(RD),
    .en(WE));
  Register register_1 (.D(DIN), .en(decoder_1_out0), .Q(R0), .clk(CLK));  // open: clr
  Register register_2 (.D(DIN), .en(decoder_1_out1), .Q(R1), .clk(CLK));  // open: clr
  Register register_3 (.D(DIN), .en(decoder_1_out2), .Q(R2), .clk(CLK));  // open: clr
  Register register_4 (.D(DIN), .en(decoder_1_out3), .Q(R3), .clk(CLK));  // open: clr
  // Probe on R0
  // Probe on R1
  // Probe on R2
  // Probe on R3
  Multiplexer #(.select(2), .width(8), .enable("false")) multiplexer_1 (
    .in0(R0), .in1(R1), .in2(R2), .in3(R3), .out(QA), .sel(RA));
  Multiplexer #(.select(2), .width(8), .enable("false")) multiplexer_2 (
    .in0(R0), .in1(R1), .in2(R2), .in3(R3), .out(QB), .sel(RB));
endmodule

module DATAPATH (
  input  [2:0] OP,
  input  [7:0] IMM,
  input  SRC,
  input  CLK,
  input  [1:0] RD,
  input  WE,
  input  [1:0] RA,
  input  [1:0] RB,
  output [7:0] R,
  output Z,
  output [7:0] R0,
  output [7:0] R1,
  output [7:0] R2,
  output [7:0] R3
);

  wire [7:0] alu8_1_r, regfile_1_qa, regfile_1_qb;

  ALU8 alu8_1 (.A(regfile_1_qa), .B(regfile_1_qb), .OP(OP), .R(alu8_1_r), .Z(Z));  // open: LT
  REGFILE regfile_1 (
    .CLK(CLK), .DIN(R), .WE(WE), .RD(RD), .QA(regfile_1_qa), .QB(regfile_1_qb), .RA(RA), .RB(RB), .R0(R0),
    .R1(R1), .R2(R2), .R3(R3));
  Multiplexer #(.width(8), .enable("false")) multiplexer_1 (.in0(alu8_1_r), .in1(IMM), .out(R), .sel(SRC));
endmodule
